# Fritzing sketch STARIZ_Schematic (saved by Fritzing 0.9.4)

parts:
  RPi4 = Raspberry Pi 3 [part_number=RPi4-Rev.1]
  Sensor1 = hc-sr04
  Sensor2 = hc-sr04
  U1 = RELAY [package=relay-g5q]

nets:
  GND: RPi4.GND, RPi4.GIPO12, RPi4.GIPO24, Sensor1.GND, Sensor2.Echo, Sensor2.GND, U1.COIL1
  N1: RPi4.GIPO5, Sensor1.Trig
  N2: RPi4.GIPO6, RPi4.GIPO13, Sensor1.Echo
  N3: RPi4.GIPO23, Sensor2.Trig
  5V: RPi4.5V, Sensor1.VCC, Sensor2.VCC, U1.COIL2

notes:
  5v Power
  5v Relay
  GND
